// Logisim project ALU.circ as structural Verilog: 11 circuits, main circuit main
module main (
  input  [7:0] in_1,
  input  in_2,
  input  [7:0] in_3,
  input  [7:0] in_4,
  output [7:0] out_5,
  output out_6,
  output out_7
);

  wire and_1_out, clock_1_out;
  wire [7:0] register_8bit_1_o, register_8bit_2_o, register_8bit_3_o;

  Clock clock_1 (.out(clock_1_out));
  and and_1 (and_1_out, clock_1_out, in_2);
  REGISTER_8bit register_8bit_1 (.DATA(in_1), .WRITE(and_1_out), .O(register_8bit_1_o));  // open: O_PRIME
  REGISTER_8bit register_8bit_2 (.DATA(in_3), .WRITE(and_1_out), .O(register_8bit_2_o));  // open: O_PRIME
  REGISTER_8bit register_8bit_3 (.DATA(in_4), .WRITE(and_1_out), .O(register_8bit_3_o));  // open: O_PRIME
  ALU alu_1 (
    .A(register_8bit_1_o), .B(register_8bit_2_o), .OPCODE(register_8bit_3_o[2:0]), .out_4(out_5),
    .OVERFLOW(out_6), .UNDERFLOW(out_7));

  // Notes on the sheet:
  //   Note: little-endian
  //   OPCODES:
  //   0x0 AND
  //   0x1 OR
  //   0x2 XOR
  //   0x3 NOT
  //   0x4 ADD
  //   0x5 SUB
endmodule

module ALU (
  input  [7:0] A,
  input  [7:0] B,
  input  [2:0] OPCODE,
  output [7:0] out_4,
  output OVERFLOW,
  output UNDERFLOW
);

  wire [7:0] adder_8bit_1_c1, and_8bit_1_c1, not_8bit_1_b1, or_8bit_1_c1, subber_8bit_1_c1, xor_8bit_1_c1;

  AND_8bit and_8bit_1 (
    .A1(A[0]), .B1(B[0]), .A2(A[1]), .B2(B[1]), .A3(A[2]), .B3(B[2]), .A4(A[3]), .B4(B[3]), .A5(A[4]),
    .B5(B[4]), .A6(A[5]), .B6(B[5]), .A7(A[6]), .B7(B[6]), .A8(A[7]), .B8(B[7]), .C1(and_8bit_1_c1[0]),
    .C2(and_8bit_1_c1[1]), .C3(and_8bit_1_c1[2]), .C4(and_8bit_1_c1[3]), .C5(and_8bit_1_c1[4]),
    .C6(and_8bit_1_c1[5]), .C7(and_8bit_1_c1[6]), .C8(and_8bit_1_c1[7]));
  OR_8bit or_8bit_1 (
    .A1(A[0]), .B1(B[0]), .A2(A[1]), .B2(B[1]), .A3(A[2]), .B3(B[2]), .A4(A[3]), .B4(B[3]), .A5(A[4]),
    .B5(B[4]), .A6(A[5]), .B6(B[5]), .A7(A[6]), .B7(B[6]), .A8(A[7]), .B8(B[7]), .C1(or_8bit_1_c1[0]),
    .C2(or_8bit_1_c1[1]), .C3(or_8bit_1_c1[2]), .C4(or_8bit_1_c1[3]), .C5(or_8bit_1_c1[4]),
    .C6(or_8bit_1_c1[5]), .C7(or_8bit_1_c1[6]), .C8(or_8bit_1_c1[7]));
  XOR_8bit xor_8bit_1 (
    .A1(A[0]), .B1(B[0]), .A2(A[1]), .B2(B[1]), .A3(A[2]), .B3(B[2]), .A4(A[3]), .B4(B[3]), .A5(A[4]),
    .B5(B[4]), .A6(A[5]), .B6(B[5]), .A7(A[6]), .B7(B[6]), .A8(A[7]), .B8(B[7]), .C1(xor_8bit_1_c1[0]),
    .C2(xor_8bit_1_c1[1]), .C3(xor_8bit_1_c1[2]), .C4(xor_8bit_1_c1[3]), .C5(xor_8bit_1_c1[4]),
    .C6(xor_8bit_1_c1[5]), .C7(xor_8bit_1_c1[6]), .C8(xor_8bit_1_c1[7]));
  NOT_8bit not_8bit_1 (
    .A1(A[0]), .A2(A[1]), .A3(A[2]), .A4(A[3]), .A5(A[4]), .A6(A[5]), .A7(A[6]), .A8(A[7]),
    .B1(not_8bit_1_b1[0]), .B2(not_8bit_1_b1[1]), .B3(not_8bit_1_b1[2]), .B4(not_8bit_1_b1[3]),
    .B5(not_8bit_1_b1[4]), .B6(not_8bit_1_b1[5]), .B7(not_8bit_1_b1[6]), .B8(not_8bit_1_b1[7]));
  ADDER_8bit adder_8bit_1 (
    .A1(A[0]), .B1(B[0]), .A2(A[1]), .B2(B[1]), .A3(A[2]), .B3(B[2]), .A4(A[3]), .B4(B[3]), .A5(A[4]),
    .B5(B[4]), .A6(A[5]), .B6(B[5]), .A7(A[6]), .B7(B[6]), .A8(A[7]), .B8(B[7]), .C1(adder_8bit_1_c1[0]),
    .C2(adder_8bit_1_c1[1]), .C3(adder_8bit_1_c1[2]), .C4(adder_8bit_1_c1[3]), .C5(adder_8bit_1_c1[4]),
    .C6(adder_8bit_1_c1[5]), .C7(adder_8bit_1_c1[6]), .C8(adder_8bit_1_c1[7]), .OVERFLOW(OVERFLOW));
  SUBBER_8bit subber_8bit_1 (
    .A1(A[0]), .B1(B[0]), .A2(A[1]), .B2(B[1]), .A3(A[2]), .B3(B[2]), .A4(A[3]), .B4(B[3]), .A5(A[4]),
    .B5(B[4]), .A6(A[5]), .B6(B[5]), .A7(A[6]), .B7(B[6]), .A8(A[7]), .B8(B[7]), .C1(subber_8bit_1_c1[0]),
    .C2(subber_8bit_1_c1[1]), .C3(subber_8bit_1_c1[2]), .C4(subber_8bit_1_c1[3]), .C5(subber_8bit_1_c1[4]),
    .C6(subber_8bit_1_c1[5]), .C7(subber_8bit_1_c1[6]), .C8(subber_8bit_1_c1[7]), .UNDERFLOW(UNDERFLOW));
  Multiplexer #(.select(3), .width(8)) multiplexer_1 (
    .in0(and_8bit_1_c1), .in1(or_8bit_1_c1), .in2(xor_8bit_1_c1), .in3(not_8bit_1_b1), .in4(adder_8bit_1_c1),
    .in5(subber_8bit_1_c1), .out(out_4), .sel(OPCODE));  // open: in6, in7
endmodule

module AND_8bit (
  input  A1,
  input  B1,
  input  A2,
  input  B2,
  input  A3,
  input  B3,
  input  A4,
  input  B4,
  input  A5,
  input  B5,
  input  A6,
  input  B6,
  input  A7,
  input  B7,
  input  A8,
  input  B8,
  output C1,
  output C2,
  output C3,
  output C4,
  output C5,
  output C6,
  output C7,
  output C8
);

  and and_1 (C1, A1, B1);
  and and_2 (C2, A2, B2);
  and and_3 (C3, A3, B3);
  and and_4 (C4, A4, B4);
  and and_5 (C5, A5, B5);
  and and_6 (C6, A6, B6);
  and and_7 (C7, A7, B7);
  and and_8 (C8, A8, B8);
endmodule

module OR_8bit (
  input  A1,
  input  B1,
  input  A2,
  input  B2,
  input  A3,
  input  B3,
  input  A4,
  input  B4,
  input  A5,
  input  B5,
  input  A6,
  input  B6,
  input  A7,
  input  B7,
  input  A8,
  input  B8,
  output C1,
  output C2,
  output C3,
  output C4,
  output C5,
  output C6,
  output C7,
  output C8
);

  or or_1 (C1, A1, B1);
  or or_2 (C2, A2, B2);
  or or_3 (C3, A3, B3);
  or or_4 (C4, A4, B4);
  or or_5 (C5, A5, B5);
  or or_6 (C6, A6, B6);
  or or_7 (C7, A7, B7);
  or or_8 (C8, A8, B8);
endmodule

module XOR_8bit (
  input  A1,
  input  B1,
  input  A2,
  input  B2,
  input  A3,
  input  B3,
  input  A4,
  input  B4,
  input  A5,
  input  B5,
  input  A6,
  input  B6,
  input  A7,
  input  B7,
  input  A8,
  input  B8,
  output C1,
  output C2,
  output C3,
  output C4,
  output C5,
  output C6,
  output C7,
  output C8
);

  xor xor_1 (C1, A1, B1);
  xor xor_2 (C2, A2, B2);
  xor xor_3 (C3, A3, B3);
  xor xor_4 (C4, A4, B4);
  xor xor_5 (C5, A5, B5);
  xor xor_6 (C6, A6, B6);
  xor xor_7 (C7, A7, B7);
  xor xor_8 (C8, A8, B8);
endmodule

module NOT_8bit (
  input  A1,
  input  A2,
  input  A3,
  input  A4,
  input  A5,
  input  A6,
  input  A7,
  input  A8,
  output B1,
  output B2,
  output B3,
  output B4,
  output B5,
  output B6,
  output B7,
  output B8
);

  not not_1 (B1, A1);
  not not_2 (B2, A2);
  not not_3 (B3, A3);
  not not_4 (B4, A4);
  not not_5 (B5, A5);
  not not_6 (B6, A6);
  not not_7 (B7, A7);
  not not_8 (B8, A8);
endmodule

module FULL_ADDER_1bit (
  input  A,
  input  B,
  input  Carry_In,
  input  SUB,
  output C,
  output Carry_Out
);

  wire and_1_out, and_2_out, xor_1_out, xor_2_out;

  xor xor_1 (xor_1_out, B, SUB);
  xor xor_2 (xor_2_out, A, xor_1_out);
  and and_1 (and_1_out, A, xor_1_out);
  and and_2 (and_2_out, xor_2_out, Carry_In);
  xor xor_3 (C, xor_2_out, Carry_In);
  or or_1 (Carry_Out, and_2_out, and_1_out);
endmodule

module SUBBER_8bit (
  input  A1,
  input  B1,
  input  A2,
  input  B2,
  input  A3,
  input  B3,
  input  A4,
  input  B4,
  input  A5,
  input  B5,
  input  A6,
  input  B6,
  input  A7,
  input  B7,
  input  A8,
  input  B8,
  output C1,
  output C2,
  output C3,
  output C4,
  output C5,
  output C6,
  output C7,
  output C8,
  output UNDERFLOW
);

  wire full_adder_1bit_1_carry_out, full_adder_1bit_2_carry_out, full_adder_1bit_3_carry_out,
       full_adder_1bit_4_carry_out, full_adder_1bit_5_carry_out, full_adder_1bit_6_carry_out,
       full_adder_1bit_7_carry_out;

  FULL_ADDER_1bit full_adder_1bit_1 (
    .A(A1), .B(B1), .Carry_In(1'b1), .SUB(1'b1), .C(C1), .Carry_Out(full_adder_1bit_1_carry_out));
  FULL_ADDER_1bit full_adder_1bit_2 (
    .A(A2), .B(B2), .Carry_In(full_adder_1bit_1_carry_out), .SUB(1'b1), .C(C2),
    .Carry_Out(full_adder_1bit_2_carry_out));
  FULL_ADDER_1bit full_adder_1bit_3 (
    .A(A3), .B(B3), .Carry_In(full_adder_1bit_2_carry_out), .SUB(1'b1), .C(C3),
    .Carry_Out(full_adder_1bit_3_carry_out));
  FULL_ADDER_1bit full_adder_1bit_4 (
    .A(A4), .B(B4), .Carry_In(full_adder_1bit_3_carry_out), .SUB(1'b1), .C(C4),
    .Carry_Out(full_adder_1bit_4_carry_out));
  FULL_ADDER_1bit full_adder_1bit_5 (
    .A(A5), .B(B5), .Carry_In(full_adder_1bit_4_carry_out), .SUB(1'b1), .C(C5),
    .Carry_Out(full_adder_1bit_5_carry_out));
  FULL_ADDER_1bit full_adder_1bit_6 (
    .A(A6), .B(B6), .Carry_In(full_adder_1bit_5_carry_out), .SUB(1'b1), .C(C6),
    .Carry_Out(full_adder_1bit_6_carry_out));
  FULL_ADDER_1bit full_adder_1bit_7 (
    .A(A7), .B(B7), .Carry_In(full_adder_1bit_6_carry_out), .SUB(1'b1), .C(C7),
    .Carry_Out(full_adder_1bit_7_carry_out));
  FULL_ADDER_1bit full_adder_1bit_8 (
    .A(A8), .B(B8), .Carry_In(full_adder_1bit_7_carry_out), .SUB(1'b1), .C(C8), .Carry_Out(UNDERFLOW));
endmodule

module ADDER_8bit (
  input  A1,
  input  B1,
  input  A2,
  input  B2,
  input  A3,
  input  B3,
  input  A4,
  input  B4,
  input  A5,
  input  B5,
  input  A6,
  input  B6,
  input  A7,
  input  B7,
  input  A8,
  input  B8,
  output C1,
  output C2,
  output C3,
  output C4,
  output C5,
  output C6,
  output C7,
  output C8,
  output OVERFLOW
);

  wire full_adder_1bit_1_carry_out, full_adder_1bit_2_carry_out, full_adder_1bit_3_carry_out,
       full_adder_1bit_4_carry_out, full_adder_1bit_5_carry_out, full_adder_1bit_6_carry_out,
       full_adder_1bit_7_carry_out;

  FULL_ADDER_1bit full_adder_1bit_1 (
    .A(A1), .B(B1), .Carry_In(1'b0), .SUB(1'b0), .C(C1), .Carry_Out(full_adder_1bit_1_carry_out));
  FULL_ADDER_1bit full_adder_1bit_2 (
    .A(A2), .B(B2), .Carry_In(full_adder_1bit_1_carry_out), .SUB(1'b0), .C(C2),
    .Carry_Out(full_adder_1bit_2_carry_out));
  FULL_ADDER_1bit full_adder_1bit_3 (
    .A(A3), .B(B3), .Carry_In(full_adder_1bit_2_carry_out), .SUB(1'b0), .C(C3),
    .Carry_Out(full_adder_1bit_3_carry_out));
  FULL_ADDER_1bit full_adder_1bit_4 (
    .A(A4), .B(B4), .Carry_In(full_adder_1bit_3_carry_out), .SUB(1'b0), .C(C4),
    .Carry_Out(full_adder_1bit_4_carry_out));
  FULL_ADDER_1bit full_adder_1bit_5 (
    .A(A5), .B(B5), .Carry_In(full_adder_1bit_4_carry_out), .SUB(1'b0), .C(C5),
    .Carry_Out(full_adder_1bit_5_carry_out));
  FULL_ADDER_1bit full_adder_1bit_6 (
    .A(A6), .B(B6), .Carry_In(full_adder_1bit_5_carry_out), .SUB(1'b0), .C(C6),
    .Carry_Out(full_adder_1bit_6_carry_out));
  FULL_ADDER_1bit full_adder_1bit_7 (
    .A(A7), .B(B7), .Carry_In(full_adder_1bit_6_carry_out), .SUB(1'b0), .C(C7),
    .Carry_Out(full_adder_1bit_7_carry_out));
  FULL_ADDER_1bit full_adder_1bit_8 (
    .A(A8), .B(B8), .Carry_In(full_adder_1bit_7_carry_out), .SUB(1'b0), .C(C8), .Carry_Out(OVERFLOW));
endmodule

module LATCH (
  input  DATA,
  input  WRITE,
  output O,
  output O_PRIME
);

  wire nand_1_out, nand_2_out, not_1_out;

  not not_1 (not_1_out, DATA);
  nand nand_1 (nand_1_out, DATA, WRITE);
  nand nand_2 (nand_2_out, WRITE, not_1_out);
  nand nand_3 (O, nand_1_out, O_PRIME);
  nand nand_4 (O_PRIME, O, nand_2_out);
endmodule

module REGISTER_8bit (
  input  [7:0] DATA,
  input  WRITE,
  output [7:0] O,
  output [7:0] O_PRIME
);

  LATCH latch_1 (.DATA(DATA[0]), .WRITE(WRITE), .O(O[0]), .O_PRIME(O_PRIME[0]));
  LATCH latch_2 (.DATA(DATA[1]), .WRITE(WRITE), .O(O[1]), .O_PRIME(O_PRIME[1]));
  LATCH latch_3 (.DATA(DATA[2]), .WRITE(WRITE), .O(O[2]), .O_PRIME(O_PRIME[2]));
  LATCH latch_4 (.DATA(DATA[3]), .WRITE(WRITE), .O(O[3]), .O_PRIME(O_PRIME[3]));
  LATCH latch_5 (.DATA(DATA[4]), .WRITE(WRITE), .O(O[4]), .O_PRIME(O_PRIME[4]));
  LATCH latch_6 (.DATA(DATA[5]), .WRITE(WRITE), .O(O[5]), .O_PRIME(O_PRIME[5]));
  LATCH latch_7 (.DATA(DATA[6]), .WRITE(WRITE), .O(O[6]), .O_PRIME(O_PRIME[6]));
  LATCH latch_8 (.DATA(DATA[7]), .WRITE(WRITE), .O(O[7]), .O_PRIME(O_PRIME[7]));
endmodule
